// Logisim project Atividade.ECOP.circ as structural Verilog: 1 circuit, main circuit main
module main (
  input  x,
  input  y,
  output a,
  output f,
  output b,
  output c,
  output d,
  output e,
  output g
);

  wire and_2_out, and_3_out, not_1_out, not_2_out, not_3_out, not_4_out, not_5_out;

  not not_1 (not_1_out, y);
  not not_2 (not_2_out, x);
  not not_3 (not_3_out, y);
  not not_4 (not_4_out, x);
  not not_5 (not_5_out, y);
  and and_1 (c, x, not_1_out);
  or or_1 (d, not_2_out, not_3_out);
  and and_2 (and_2_out, not_4_out, not_5_out);
  and and_3 (and_3_out, x, y);
  or or_2 (g, and_2_out, and_3_out);
  _7_Segment_Display u_7_segment_display_1 (.g(g), .f(1'b1), .a(1'b1), .b(x), .e(1'b1), .d(d), .c(c));  // open: dp

  assign a = 1'b1;
  assign b = x;
  assign e = 1'b1;
  assign f = 1'b1;
endmodule
