// Logisim project Lista de Circuitos.2.circ as structural Verilog
module Soma (
  input  [3:0] A,
  input  [3:0] B,
  output [3:0] C,
  output out_4
);

  Adder #(.width(4)) adder_1 (.a(A), .b(B), .out(C), .cout(out_4));  // open: cin
endmodule

module \Subtração  (
  input  [3:0] in_1,
  input  [3:0] in_2,
  output [3:0] out_3,
  output out_4
);

  Subtractor #(.width(4)) subtractor_1 (.a(in_1), .b(in_2), .out(out_3), .bout(out_4));  // open: bin
endmodule

module AND (
  input  [3:0] in_1,
  input  [3:0] in_2,
  output [3:0] out_3
);

  assign out_3 = in_1 & in_2;  // AND_Gate and_1, 4 bits wide
endmodule

module XOR (
  input  [3:0] in_1,
  input  [3:0] in_2,
  output [3:0] out_3
);

  assign out_3 = in_1 ^ in_2;  // XOR_Gate xor_1, 4 bits wide
endmodule

module MUX (
  input  [3:0] A,
  input  [3:0] B,
  input  [1:0] in_3,
  output out_4,
  output [3:0] C,
  output [3:0] A_2,
  output [3:0] B_2
);

  wire [3:0] and_1_out_3, soma_1_c, \subtração_1_out_3 , xor_1_out_3;

  Soma soma_1 (.A(A), .B(B), .out_4(out_4), .C(soma_1_c));
  \Subtração  \subtração_1  (.in_1(A), .in_2(B), .out_3(\subtração_1_out_3 ));  // open: out_4
  AND and_1 (.in_1(A), .in_2(B), .out_3(and_1_out_3));
  XOR xor_1 (.in_1(A), .in_2(B), .out_3(xor_1_out_3));
  Multiplexer #(.select(2), .width(4)) multiplexer_1 (
    .in0(soma_1_c), .in1(\subtração_1_out_3 ), .in2(and_1_out_3), .in3(xor_1_out_3), .out(C), .sel(in_3));  // open: en

  assign A_2 = A;
  assign B_2 = B;

  // Notes on the sheet:
  //   B: pull=down
endmodule

module Principal (
  input  [3:0] Entrada_A,
  input  [3:0] Entrada_B,
  input  [1:0] Seletor_S1_S0
);

  wire mux_1_out_4;
  wire [3:0] mux_1_a_2, mux_1_b_2, mux_1_c;

  LED OVERFLOW (.in(mux_1_out_4));
  MUX mux_1 (
    .A(Entrada_A), .B(Entrada_B), .out_4(mux_1_out_4), .in_3(Seletor_S1_S0), .C(mux_1_c), .A_2(mux_1_a_2),
    .B_2(mux_1_b_2));
  Hex_Digit_Display hex_digit_display_1 (.value(mux_1_a_2));  // open: dp
  Hex_Digit_Display hex_digit_display_2 (.value(mux_1_b_2));  // open: dp
  Hex_Digit_Display hex_digit_display_3 (.value(mux_1_c));  // open: dp
endmodule
